# Fritzing sketch Herba-Automata (saved by Fritzing 0.9.3b)
breadboards: 1

parts:
  Part1 = Arduino Nano (Rev3.0)
  U1 = 4-Channel 5v Relay Shield [package=relay-4ch5v10a]
  Part2 = Soil Moisture Sensor
  DHT1 = DHT11 Humitidy and Temperature Sensor

nets (from the schematic view):
  GND: Part1.GND, U1.GND, Part2.GND, DHT1.GND
  N1: Part1.D2, DHT1.DATA
  N2: Part1.D3, Part2.SIG
  N3: Part1.D4, U1.K1-On, U1.K3-On
  5V: Part1.VIN, Part2.VCC, DHT1.VDD

custom parts:
  4-Channel 5v Relay Shield: 4 Channel 5v Relay Shield w. 2x SPD-06VDC-SD-C
  DHT11 Humitidy and Temperature Sensor: DHT11 Humidity and Temperature Sensor

// code stored in the sketch: Herba-Automata.ino



/*
 * 
 * Welcome to Herba-Automata!
 * ~~~~~~~~~~~~~~~~~~~~~~~~~~
 * 
 * Created by Willie Phistterbut @PhistterbutInc or on thingiverse at thingiverse.com/phistterbut_inc/about
 * 
 * This firmware designed to control lighting, irrigation and a set of sensors for automated
 * indoor/outdoor farming using embedded systems
 * 
 * Released under MIT license.
 * Distibute/modify freely with attribution
 * 
 * 
 * Planned Features:
 * ~~~~~~~~~~~~~~~~~
 * support for multiple Arduino based boards (nano, mega, pro and duo at least)
 * 
 * sensor interaction, including
 * daylight, moisture, air temp, humidity, maybe soil temp (cheap source?)
 * 
 * relay interaction for lights and irrigation
 * 
 * customizable data logging
 * 
 * automated construction of spreadsheet information (??maybe??) 
 * 
 * internet capabilities, web page?
 * 
 * LCD screen support: 16x2, 16x4 i2c modules
 * 
 * Hardware Planned/Required:
 * ~~~~~~~~~~~~~~~~~~~~~~~~~~
 * Arduino board
 * Soil moisture sensor
 * Real time clock (premade OTS comp. or IC???)
 * Relay/s, Required for water/light control
 * Photoresistor, Optional, for logging sun data
 * Air temp./Humidity sensor, Optional
 * 
 * 
 *
 * 
 * 
 * 
 * 
 * Included Features:
 * ~~~~~~~~~~~~~~~~~~
 * Pretty much jack squat... except this page, I guess
 * 
 * hardware to come first!
 * 
*/

void setup() {
  // put your setup code here, to run once:
//TODO: add code to setup
}

void loop() {
  // put your main code here, to run repeatedly:
//TODO: add code to loop
}
